// Logisim project BancoReg.circ as structural Verilog: 2 circuits, main circuit main
module main (
  input  [3:0] R1Addr,
  input  [31:0] DataWrite,
  input  [3:0] RegAddr,
  input  [3:0] R2Addr,
  input  EW,
  input  CLK,
  output [31:0] R1,
  output [31:0] R2
);

  wire [31:0] demultiplexer_1_out1, demultiplexer_1_out2, demultiplexer_1_out3, demultiplexer_1_out4,
       demultiplexer_1_out5, demultiplexer_1_out6, demultiplexer_1_out7, demultiplexer_1_out8,
       demultiplexer_1_out9, demultiplexer_1_out10, demultiplexer_1_out11, demultiplexer_1_out12,
       demultiplexer_1_out13, demultiplexer_1_out14, demultiplexer_1_out15, registrador_1_query,
       registrador_2_query, registrador_3_query, registrador_4_query, registrador_5_query,
       registrador_6_query, registrador_7_query, registrador_8_query, registrador_9_query,
       registrador_10_query, registrador_11_query, registrador_12_query, registrador_13_query,
       registrador_14_query, registrador_15_query, registrador_16_query;

  Demultiplexer #(.select(4), .width(32)) demultiplexer_1 (
    .out1(demultiplexer_1_out1), .out2(demultiplexer_1_out2), .out3(demultiplexer_1_out3),
    .out4(demultiplexer_1_out4), .out5(demultiplexer_1_out5), .out6(demultiplexer_1_out6),
    .out7(demultiplexer_1_out7), .out8(demultiplexer_1_out8), .out9(demultiplexer_1_out9),
    .out10(demultiplexer_1_out10), .out11(demultiplexer_1_out11), .out12(demultiplexer_1_out12),
    .out13(demultiplexer_1_out13), .out14(demultiplexer_1_out14), .out15(demultiplexer_1_out15),
    .in(DataWrite), .sel(RegAddr));  // open: out0
  Registrador registrador_1 (.Data({32{1'b0}}), .WE(EW), .CLK(CLK), .Query(registrador_1_query));
  Registrador registrador_2 (.Data(demultiplexer_1_out1), .WE(EW), .CLK(CLK), .Query(registrador_2_query));
  Registrador registrador_3 (.Data(demultiplexer_1_out2), .WE(EW), .CLK(CLK), .Query(registrador_3_query));
  Registrador registrador_4 (.Data(demultiplexer_1_out3), .WE(EW), .CLK(CLK), .Query(registrador_4_query));
  Registrador registrador_5 (.Data(demultiplexer_1_out4), .WE(EW), .CLK(CLK), .Query(registrador_5_query));
  Registrador registrador_6 (.Data(demultiplexer_1_out5), .WE(EW), .CLK(CLK), .Query(registrador_6_query));
  Registrador registrador_7 (.Data(demultiplexer_1_out6), .WE(EW), .CLK(CLK), .Query(registrador_7_query));
  Registrador registrador_8 (.Data(demultiplexer_1_out7), .WE(EW), .CLK(CLK), .Query(registrador_8_query));
  Registrador registrador_9 (.Data(demultiplexer_1_out8), .WE(EW), .CLK(CLK), .Query(registrador_9_query));
  Registrador registrador_10 (.Data(demultiplexer_1_out9), .WE(EW), .CLK(CLK), .Query(registrador_10_query));
  Registrador registrador_11 (.Data(demultiplexer_1_out10), .WE(EW), .CLK(CLK), .Query(registrador_11_query));
  Registrador registrador_12 (.Data(demultiplexer_1_out11), .WE(EW), .CLK(CLK), .Query(registrador_12_query));
  Registrador registrador_13 (.Data(demultiplexer_1_out12), .WE(EW), .CLK(CLK), .Query(registrador_13_query));
  Registrador registrador_14 (.Data(demultiplexer_1_out13), .WE(EW), .CLK(CLK), .Query(registrador_14_query));
  Registrador registrador_15 (.Data(demultiplexer_1_out14), .WE(EW), .CLK(CLK), .Query(registrador_15_query));
  Registrador registrador_16 (.Data(demultiplexer_1_out15), .WE(EW), .CLK(CLK), .Query(registrador_16_query));
  Multiplexer #(.select(4), .width(32)) multiplexer_1 (
    .in0(registrador_1_query), .in1(registrador_2_query), .in2(registrador_3_query),
    .in3(registrador_4_query), .in4(registrador_5_query), .in5(registrador_6_query),
    .in6(registrador_7_query), .in7(registrador_8_query), .in8(registrador_9_query),
    .in9(registrador_10_query), .in10(registrador_11_query), .in11(registrador_12_query),
    .in12(registrador_13_query), .in13(registrador_14_query), .in14(registrador_15_query),
    .in15(registrador_16_query), .out(R1), .sel(R1Addr));
  Multiplexer #(.select(4), .width(32)) multiplexer_2 (
    .in0(registrador_1_query), .in1(registrador_2_query), .in2(registrador_3_query),
    .in3(registrador_4_query), .in4(registrador_5_query), .in5(registrador_6_query),
    .in6(registrador_7_query), .in7(registrador_8_query), .in8(registrador_9_query),
    .in9(registrador_10_query), .in10(registrador_11_query), .in11(registrador_12_query),
    .in12(registrador_13_query), .in13(registrador_14_query), .in14(registrador_15_query),
    .in15(registrador_16_query), .out(R2), .sel(R2Addr));

  // Notes on the sheet:
  //   X0
  //   x1
  //   x2
  //   x3
  //   x4
  //   x5
  //   x6
  //   x7
  //   x8
  //   x9
  //   xA
  //   xB
  //   xC
  //   xD
  //   xE
  //   XF
endmodule

module Registrador (
  input  [31:0] Data,
  input  WE,
  input  CLK,
  output [31:0] Query
);

  wire nor_1_out;

  nor nor_1 (nor_1_out, WE, ~CLK);  // NOR_Gate
  D_Flip_Flop d_ff_1 (.D(Data[31]), .clk(nor_1_out), .Q(Query[31]));  // open: Qn, preset, reset
  D_Flip_Flop d_ff_2 (.D(Data[30]), .clk(nor_1_out), .Q(Query[30]));  // open: Qn, preset, reset
  D_Flip_Flop d_ff_3 (.D(Data[29]), .clk(nor_1_out), .Q(Query[29]));  // open: Qn, preset, reset
  D_Flip_Flop d_ff_4 (.D(Data[28]), .clk(nor_1_out), .Q(Query[28]));  // open: Qn, preset, reset
  D_Flip_Flop d_ff_5 (.D(Data[27]), .clk(nor_1_out), .Q(Query[27]));  // open: Qn, preset, reset
  D_Flip_Flop d_ff_6 (.D(Data[26]), .clk(nor_1_out), .Q(Query[26]));  // open: Qn, preset, reset
  D_Flip_Flop d_ff_7 (.D(Data[25]), .clk(nor_1_out), .Q(Query[25]));  // open: Qn, preset, reset
  D_Flip_Flop d_ff_8 (.D(Data[24]), .clk(nor_1_out), .Q(Query[24]));  // open: Qn, preset, reset
  D_Flip_Flop d_ff_9 (.D(Data[23]), .clk(nor_1_out), .Q(Query[23]));  // open: Qn, preset, reset
  D_Flip_Flop d_ff_10 (.D(Data[22]), .clk(nor_1_out), .Q(Query[22]));  // open: Qn, preset, reset
  D_Flip_Flop d_ff_11 (.D(Data[21]), .clk(nor_1_out), .Q(Query[21]));  // open: Qn, preset, reset
  D_Flip_Flop d_ff_12 (.D(Data[20]), .clk(nor_1_out), .Q(Query[20]));  // open: Qn, preset, reset
  D_Flip_Flop d_ff_13 (.D(Data[19]), .clk(nor_1_out), .Q(Query[19]));  // open: Qn, preset, reset
  D_Flip_Flop d_ff_14 (.D(Data[18]), .clk(nor_1_out), .Q(Query[18]));  // open: Qn, preset, reset
  D_Flip_Flop d_ff_15 (.D(Data[17]), .clk(nor_1_out), .Q(Query[17]));  // open: Qn, preset, reset
  D_Flip_Flop d_ff_16 (.D(Data[16]), .clk(nor_1_out), .Q(Query[16]));  // open: Qn, preset, reset
  D_Flip_Flop d_ff_17 (.D(Data[15]), .Q(Query[15]));  // open: clk, Qn, preset, reset
  D_Flip_Flop d_ff_18 (.D(Data[14]), .clk(nor_1_out), .Q(Query[14]));  // open: Qn, preset, reset
  D_Flip_Flop d_ff_19 (.D(Data[13]), .clk(nor_1_out), .Q(Query[13]));  // open: Qn, preset, reset
  D_Flip_Flop d_ff_20 (.D(Data[12]), .clk(nor_1_out), .Q(Query[12]));  // open: Qn, preset, reset
  D_Flip_Flop d_ff_21 (.D(Data[11]), .clk(nor_1_out), .Q(Query[11]));  // open: Qn, preset, reset
  D_Flip_Flop d_ff_22 (.D(Data[10]), .clk(nor_1_out), .Q(Query[10]));  // open: Qn, preset, reset
  D_Flip_Flop d_ff_23 (.D(Data[9]), .clk(nor_1_out), .Q(Query[9]));  // open: Qn, preset, reset
  D_Flip_Flop d_ff_24 (.D(Data[8]), .clk(nor_1_out), .Q(Query[8]));  // open: Qn, preset, reset
  D_Flip_Flop d_ff_25 (.D(Data[7]), .clk(nor_1_out), .Q(Query[7]));  // open: Qn, preset, reset
  D_Flip_Flop d_ff_26 (.D(Data[6]), .clk(nor_1_out), .Q(Query[6]));  // open: Qn, preset, reset
  D_Flip_Flop d_ff_27 (.D(Data[5]), .clk(nor_1_out), .Q(Query[5]));  // open: Qn, preset, reset
  D_Flip_Flop d_ff_28 (.D(Data[4]), .clk(nor_1_out), .Q(Query[4]));  // open: Qn, preset, reset
  D_Flip_Flop d_ff_29 (.D(Data[3]), .clk(nor_1_out), .Q(Query[3]));  // open: Qn, preset, reset
  D_Flip_Flop d_ff_30 (.D(Data[2]), .clk(nor_1_out), .Q(Query[2]));  // open: Qn, preset, reset
  D_Flip_Flop d_ff_31 (.D(Data[1]), .clk(nor_1_out), .Q(Query[1]));  // open: Qn, preset, reset
  D_Flip_Flop d_ff_32 (.D(Data[0]), .clk(nor_1_out), .Q(Query[0]));  // open: Qn, preset, reset
endmodule
