// Logisim project MemInstrucao.circ as structural Verilog: 1 circuit, main circuit main
module main (
  input  [3:0] ADDR,
  output [15:0] Ins
);

  wire [3:3] undriven;

  ROM #(.addrWidth(4), .dataWidth(16)) rom_1 (.addr({undriven[3], ADDR[3:1]}), .data(Ins));
endmodule
