// Logisim project MemoriaInst.circ as structural Verilog: 1 circuit, main circuit main
module main (
  input  [4:0] in_1,
  output [7:0] out_2
);

  wire [4:4] undriven;

  ROM #(.addrWidth(5)) rom_1 (.addr({undriven[4], in_1[4:1]}), .data(out_2));
endmodule
