// Logisim project ULA.circ as structural Verilog: 4 circuits, main circuit main
module main (
  input  [31:0] A,
  input  [31:0] B,
  input  [1:0] Op,
  output [31:0] Result,
  output Zero
);

  wire and_1_out, and_2_out, and_3_out, and_4_out, and_5_out, and_6_out, and_13_out, and_14_out,
       coletor_1_out_2, comparador_1_out_2;
  wire [31:0] adder_1_out, and_7_out, and_8_out, and_9_out, and_10_out, and_11_out, and_12_out,
       distribuidor_1_out_2, distribuidor_2_out_2, distribuidor_3_out_2, distribuidor_4_out_2, or_1_out,
       subtractor_1_out;

  and and_1 (and_1_out, ~Op[0], ~Op[1]);  // AND_Gate
  and and_2 (and_2_out, Op[0], ~Op[1]);  // AND_Gate
  and and_3 (and_3_out, ~Op[0], Op[1]);  // AND_Gate
  and and_4 (and_4_out, Op[0], Op[1]);
  and and_5 (and_5_out, ~Op[0], ~Op[1]);  // AND_Gate
  and and_6 (and_6_out, Op[0], ~Op[1]);  // AND_Gate
  assign or_1_out = A | B;  // OR_Gate or_1, 32 bits wide
  distribuidor distribuidor_1 (.in_1(and_1_out), .out_2(distribuidor_1_out_2));
  assign and_7_out = A & B;  // AND_Gate and_7, 32 bits wide
  distribuidor distribuidor_2 (.in_1(and_2_out), .out_2(distribuidor_2_out_2));
  distribuidor distribuidor_3 (.in_1(and_3_out), .out_2(distribuidor_3_out_2));
  Adder #(.width(32)) adder_1 (.a(A), .b(B), .out(adder_1_out));  // open: cin, cout
  Subtractor #(.width(32)) subtractor_1 (.a(A), .b(B), .out(subtractor_1_out));  // open: bin, bout
  distribuidor distribuidor_4 (.in_1(and_4_out), .out_2(distribuidor_4_out_2));
  assign and_8_out = or_1_out & distribuidor_1_out_2;  // AND_Gate and_8, 32 bits wide
  assign and_9_out = and_7_out & distribuidor_2_out_2;  // AND_Gate and_9, 32 bits wide
  assign and_10_out = adder_1_out & distribuidor_3_out_2;  // AND_Gate and_10, 32 bits wide
  assign and_11_out = subtractor_1_out & distribuidor_4_out_2;  // AND_Gate and_11, 32 bits wide
  comparador comparador_1 (.in_1(subtractor_1_out), .out_2(comparador_1_out_2));
  assign and_12_out = ~subtractor_1_out & ~{32{1'b0}};  // AND_Gate and_12, 32 bits wide
  coletor coletor_1 (.in_1(and_12_out), .out_2(coletor_1_out_2));
  assign Result = and_8_out | and_9_out | and_10_out | and_11_out;  // OR_Gate or_2, 32 bits wide
  and and_13 (and_13_out, and_5_out, comparador_1_out_2);
  and and_14 (and_14_out, coletor_1_out_2, and_6_out);
  or or_3 (Zero, and_13_out, and_14_out);
endmodule

module distribuidor (
  input  in_1,
  output [31:0] out_2
);


  assign out_2 = {32{in_1}};
endmodule

module coletor (
  input  [31:0] in_1,
  output out_2
);


  assign out_2 = in_1[31];
endmodule

module comparador (
  input  [31:0] in_1,
  output out_2
);

  nor nor_1 (out_2, in_1[0], in_1[1], in_1[2], in_1[3], in_1[4], in_1[5], in_1[6], in_1[7], in_1[8], in_1[9], in_1[10], in_1[11], in_1[12], in_1[13], in_1[14], in_1[15], in_1[16], in_1[17], in_1[18], in_1[19], in_1[20], in_1[21], in_1[22], in_1[23], in_1[24], in_1[25], in_1[26], in_1[27], in_1[28], in_1[29], in_1[30], in_1[31]);
endmodule
